# Fritzing sketch WebMonitoringSystem (saved by Fritzing 0.9.1b)
breadboards: 1

parts:
  Часть1 = Arduino Ethernet Shield (Rev3)
  Часть2 = Arduino Uno (Rev3)
  U1 = PIR Sensor HC-SR501
  RHT1 = Humidity and Temperature Sensor RHT03
  Часть3 = BH1750FVI Breakout Board [part_number=BH1750FVI]
  Часть4 = FC-28 Soil Hygrometer Module
  U2 = GAS_SENSOR [package=mq-3]
  KY-1 = Keyes Relay [package=THT]

nets:
  N1: Часть1.A0, RHT1.Data-signal
  N2: Часть1.A1, U2.H2
  N3: Часть1.A3, Часть4.AO
  N4: Часть1.A5/SCL, Часть3.SCL
  N5: Часть1.PWM_D5, U1.OUT
  N6: Часть1.D7, KY-1.signal
  VCC: Часть1.5V, U1.VCC, RHT1.Vcc, Часть3.VCC, Часть4.VCC, KY-1.power
  GND: Часть1.GND, U1.GND, RHT1.GND_2, Часть3.GND, Часть4.GND, U2.H1, KY-1.ground
  N7: Часть2.A4/SDA, Часть3.SDA

custom parts:
  PIR Sensor HC-SR501: Passive Infra-Red (PIR) sensor HC-SR501
  BH1750FVI Breakout Board: The ROHM Semiconductor BH1750FVI is a digital ambient light sensor for the I2C bus interface. The BH750FVI is able to detect a wide range of light intensities (1-65535 lux). The spectral range is similar to that of the human eye.
  FC-28 Soil Hygrometer Module: The FC-28 is a soil hygrometer module that uses the Texas Instruments LM393 comparator chip to provide an analog measurement of soil humidity. The digital output is high when soil moisture is over a certain threshold, as determined by adjusting the potentiometer.
  Keyes Relay: The Keyes 5V relay module is suitable for SCM development, home appliance control. It uses a 5V~12V TIL control signal which can control DC / AC signal.
